// Logisim project Guia0603(B).circ as structural Verilog
module Guia_0601 (
  input  X,
  input  Y,
  input  Z,
  input  X_2,
  input  Y_2,
  input  Z_2,
  input  X_3,
  input  Y_3,
  input  Z_3,
  input  X_4,
  input  Y_4,
  input  Z_4,
  input  X_5,
  input  Y_5,
  input  Z_5,
  output out_16,
  output out_17,
  output out_18,
  output out_19,
  output out_20
);

  wire and_1_out, and_2_out, and_3_out, and_4_out, and_5_out, and_6_out, and_7_out, and_8_out, and_9_out,
       and_10_out, and_11_out, not_1_out, not_2_out, not_3_out, not_4_out, not_5_out, not_6_out, not_7_out;

  not not_1 (not_1_out, Y);
  not not_2 (not_2_out, X_2);
  not not_3 (not_3_out, Z_2);
  not not_4 (not_4_out, Z_3);
  not not_5 (not_5_out, Z_3);
  not not_6 (not_6_out, X_4);
  not not_7 (not_7_out, Z_4);
  and and_1 (and_1_out, not_1_out, Z);
  and and_2 (and_2_out, X, Z);
  and and_3 (and_3_out, not_2_out, Y_2);
  and and_4 (and_4_out, Y_2, not_3_out);
  and and_5 (and_5_out, Y_3, not_4_out);
  and and_6 (and_6_out, X_3, Y_3);
  and and_7 (and_7_out, X_3, not_5_out);
  and and_8 (and_8_out, not_6_out, Y_4);
  and and_9 (and_9_out, Y_4, not_7_out);
  and and_10 (and_10_out, Y_5, Z_5);
  and and_11 (and_11_out, X_5, Z_5);
  or or_1 (out_16, and_1_out, and_2_out);
  or or_2 (out_17, and_3_out, and_4_out);
  or or_3 (out_18, and_5_out, and_6_out, and_7_out);
  or or_4 (out_19, and_8_out, and_9_out);
  or or_5 (out_20, and_10_out, and_11_out);

  // Notes on the sheet:
  //   A)(y' . z) + (x . z)
  //   B) (x'.y) + (y . z')
  //   D) (x' . y) + (y . z')
  //   E) (y . z) + (x . z)
  //   C) (y . z') + (x . y) + (x . z')
endmodule

module Guia0602 (
  input  X,
  input  Y,
  input  Z,
  input  X_2,
  input  Y_2,
  input  Z_2,
  input  X_3,
  input  Y_3,
  input  Z_3,
  input  X_4,
  input  Y_4,
  input  Z_4,
  input  X_5,
  input  Y_5,
  input  Z_5,
  output out_16,
  output out_17,
  output out_18,
  output out_19,
  output out_20
);

  wire not_1_out, not_2_out, not_3_out, not_4_out, not_5_out, not_6_out, not_7_out, not_8_out, not_9_out,
       not_10_out, not_11_out, not_12_out, not_13_out, or_1_out, or_2_out, or_3_out, or_4_out, or_5_out,
       or_6_out, or_7_out, or_8_out, or_9_out, or_10_out, or_11_out;

  not not_1 (not_1_out, X);
  not not_2 (not_2_out, X);
  not not_3 (not_3_out, Y);
  not not_4 (not_4_out, Z_2);
  not not_5 (not_5_out, X_2);
  not not_6 (not_6_out, Z_2);
  not not_7 (not_7_out, Y_3);
  not not_8 (not_8_out, Z_3);
  not not_9 (not_9_out, Z_3);
  not not_10 (not_10_out, Y_4);
  not not_11 (not_11_out, Y_5);
  not not_12 (not_12_out, X_5);
  not not_13 (not_13_out, Y_5);
  or or_1 (or_1_out, not_1_out, Z);
  or or_2 (or_2_out, not_2_out, not_3_out);
  or or_3 (or_3_out, Y_2, not_4_out);
  or or_4 (or_4_out, not_5_out, not_6_out);
  or or_5 (or_5_out, X_3, not_7_out);
  or or_6 (or_6_out, Y_3, not_8_out);
  or or_7 (or_7_out, X_3, not_9_out);
  or or_8 (or_8_out, Y_4, Z_4);
  or or_9 (or_9_out, not_10_out, Z_4);
  or or_10 (or_10_out, not_11_out, Z_5);
  or or_11 (or_11_out, not_12_out, not_13_out);
  and and_1 (out_16, or_1_out, or_2_out);
  and and_2 (out_17, or_3_out, or_4_out);
  and and_3 (out_18, or_5_out, or_6_out, or_7_out);
  and and_4 (out_19, or_8_out, or_9_out);
  and and_5 (out_20, or_10_out, or_11_out);

  // Notes on the sheet:
  //   A) (X' + Z) . (X' + Y')
  //   B) (Y + Z') . (X' +Z')
  //   D) (Y + Z) . (Y' + Z)
  //   E) (Y' + Z) . (X' + Y')
  //   C) (X + Y') . (Y + Z') . (X + Z')
endmodule

module Guia0603_A (
  input  X,
  input  Y,
  input  W,
  input  Z,
  output out_5
);

  wire and_1_out, and_2_out, and_3_out, and_4_out, and_5_out, and_6_out, and_7_out, and_8_out, not_1_out,
       not_2_out, not_3_out, not_4_out, not_5_out, not_6_out, not_7_out, not_8_out, or_1_out, or_2_out,
       or_3_out, or_4_out, or_5_out, or_6_out;

  not not_1 (not_1_out, X);
  not not_2 (not_2_out, Y);
  not not_3 (not_3_out, W);
  not not_4 (not_4_out, X);
  not not_5 (not_5_out, X);
  not not_6 (not_6_out, Z);
  not not_7 (not_7_out, Y);
  not not_8 (not_8_out, Y);
  and and_1 (and_1_out, not_1_out, Y);
  and and_2 (and_2_out, not_2_out, not_3_out);
  and and_3 (and_3_out, not_4_out, Z);
  and and_4 (and_4_out, not_5_out, Y, W);
  and and_5 (and_5_out, W, not_6_out);
  and and_6 (and_6_out, W, Z);
  and and_7 (and_7_out, not_7_out, W);
  and and_8 (and_8_out, X, not_8_out);
  or or_1 (or_1_out, and_1_out, and_2_out);
  or or_2 (or_2_out, and_3_out, and_4_out);
  or or_3 (or_3_out, and_5_out, and_6_out);
  or or_4 (or_4_out, and_7_out, and_8_out);
  or or_5 (or_5_out, or_1_out, or_2_out);
  or or_6 (or_6_out, or_3_out, or_4_out);
  or or_7 (out_5, or_5_out, or_6_out);

  // Notes on the sheet:
  //   A) (x'. y) + (y' . w') + (x' . z) + (x'.y . w) + (w. z') + (w. z) + (y'. w) + (x . y')
endmodule

module Guia0603_B (
  input  X,
  input  Y,
  input  W,
  input  Z,
  output out_5
);

  wire and_1_out, and_2_out, and_3_out, and_4_out, and_5_out, and_6_out, and_7_out, not_1_out, not_2_out,
       not_3_out, not_4_out, not_5_out, not_6_out, not_7_out, not_8_out, not_9_out, not_10_out, not_11_out,
       not_12_out, not_13_out, or_1_out, or_2_out, or_3_out, or_4_out, or_5_out;

  not not_1 (not_1_out, X);
  not not_2 (not_2_out, Y);
  not not_3 (not_3_out, Z);
  not not_4 (not_4_out, X);
  not not_5 (not_5_out, Y);
  not not_6 (not_6_out, Z);
  not not_7 (not_7_out, Y);
  not not_8 (not_8_out, W);
  not not_9 (not_9_out, Y);
  not not_10 (not_10_out, W);
  not not_11 (not_11_out, Y);
  not not_12 (not_12_out, W);
  not not_13 (not_13_out, W);
  and and_1 (and_1_out, not_1_out, not_2_out, not_3_out);
  and and_2 (and_2_out, not_4_out, not_5_out, W);
  and and_3 (and_3_out, W, not_6_out);
  and and_4 (and_4_out, not_7_out, not_8_out);
  and and_5 (and_5_out, not_9_out, not_10_out);
  and and_6 (and_6_out, not_11_out, not_12_out);
  and and_7 (and_7_out, X, not_13_out, Z);
  or or_1 (or_1_out, and_1_out, and_2_out);
  or or_2 (or_2_out, and_3_out, and_4_out);
  or or_3 (or_3_out, and_5_out, and_6_out);
  or or_4 (or_4_out, or_1_out, or_2_out);
  or or_5 (or_5_out, or_3_out, and_7_out);
  or or_6 (out_5, or_4_out, or_5_out);

  // Notes on the sheet:
  //   B) (x' . y' . z') + (x' . y' . w) + (w . z') + (y' . w') + (y' . w') + (y' . w') + (x . w' . z)
endmodule

module Guia0603_C (
  input  X,
  input  Y,
  input  W,
  input  Z,
  output out_5
);

  wire and_1_out, and_2_out, and_3_out, and_4_out, and_5_out, and_6_out, and_7_out, and_8_out, and_9_out,
       and_10_out, and_11_out, not_1_out, not_2_out, not_3_out, not_4_out, not_5_out, not_6_out, not_7_out,
       not_8_out, not_9_out, not_10_out, not_11_out, not_12_out, not_13_out, not_14_out, not_15_out,
       not_16_out, not_17_out, not_18_out, not_19_out, not_20_out, not_21_out, not_22_out, not_23_out,
       or_1_out, or_2_out, or_3_out, or_4_out, or_5_out, or_6_out, or_7_out, or_8_out;

  not not_1 (not_1_out, X);
  not not_2 (not_2_out, Y);
  not not_3 (not_3_out, W);
  not not_4 (not_4_out, Y);
  not not_5 (not_5_out, W);
  not not_6 (not_6_out, X);
  not not_7 (not_7_out, Y);
  not not_8 (not_8_out, W);
  not not_9 (not_9_out, W);
  not not_10 (not_10_out, Z);
  not not_11 (not_11_out, X);
  not not_12 (not_12_out, Y);
  not not_13 (not_13_out, W);
  not not_14 (not_14_out, X);
  not not_15 (not_15_out, W);
  not not_16 (not_16_out, Z);
  not not_17 (not_17_out, Y);
  not not_18 (not_18_out, W);
  not not_19 (not_19_out, Y);
  not not_20 (not_20_out, W);
  not not_21 (not_21_out, W);
  not not_22 (not_22_out, Z);
  not not_23 (not_23_out, Y);
  and and_1 (and_1_out, not_1_out, not_2_out, not_3_out);
  and and_2 (and_2_out, not_4_out, not_5_out);
  and and_3 (and_3_out, not_6_out, not_7_out, not_8_out);
  and and_4 (and_4_out, not_9_out, not_10_out);
  and and_5 (and_5_out, not_11_out, not_12_out, not_13_out);
  and and_6 (and_6_out, not_14_out, not_15_out, not_16_out);
  and and_7 (and_7_out, not_17_out, not_18_out);
  and and_8 (and_8_out, not_19_out, not_20_out);
  and and_9 (and_9_out, Y, W);
  and and_10 (and_10_out, not_21_out, not_22_out);
  and and_11 (and_11_out, X, not_23_out);
  or or_1 (or_1_out, and_1_out, and_2_out);
  or or_2 (or_2_out, and_3_out, and_4_out);
  or or_3 (or_3_out, and_5_out, and_6_out);
  or or_4 (or_4_out, and_7_out, and_8_out);
  or or_5 (or_5_out, and_9_out, and_10_out);
  or or_6 (or_6_out, or_1_out, or_2_out);
  or or_7 (or_7_out, or_3_out, or_4_out);
  or or_8 (or_8_out, or_5_out, and_11_out);
  or or_9 (out_5, or_6_out, or_7_out, or_8_out);

  // Notes on the sheet:
  //   C) (x' . y' . w') + (y' . w') + (x' . y' . w' ) + (w' . z') + (x' . y' . w' ) + (y' . w' . z') + (y' . w' ) + (y' . w' ) + (y . w ) + (w' . z') + (x . y' )
endmodule

module Guia0603_D (
  input  X,
  input  Y,
  input  W,
  input  Z,
  output out_5
);

  wire and_1_out, and_2_out, and_3_out, and_4_out, and_5_out, and_6_out, and_7_out, and_8_out, and_9_out,
       and_10_out, not_1_out, not_2_out, not_3_out, not_4_out, not_5_out, not_6_out, not_7_out, not_8_out,
       not_9_out, not_10_out, not_11_out, or_1_out, or_2_out, or_3_out, or_4_out, or_5_out, or_6_out,
       or_7_out, or_8_out;

  not not_1 (not_1_out, Y);
  not not_2 (not_2_out, Z);
  not not_3 (not_3_out, X);
  not not_4 (not_4_out, W);
  not not_5 (not_5_out, W);
  not not_6 (not_6_out, Z);
  not not_7 (not_7_out, X);
  not not_8 (not_8_out, X);
  not not_9 (not_9_out, Z);
  not not_10 (not_10_out, Z);
  not not_11 (not_11_out, Z);
  and and_1 (and_1_out, not_1_out, W, not_2_out);
  and and_2 (and_2_out, not_3_out, Y, not_4_out);
  and and_3 (and_3_out, Y, not_5_out, not_6_out);
  and and_4 (and_4_out, not_7_out, Y);
  and and_5 (and_5_out, Y, W);
  and and_6 (and_6_out, Y, W);
  and and_7 (and_7_out, not_8_out, Z);
  and and_8 (and_8_out, X, W, not_9_out);
  and and_9 (and_9_out, X, Y, not_10_out);
  and and_10 (and_10_out, W, not_11_out);
  or or_1 (or_1_out, and_1_out, and_2_out);
  or or_2 (or_2_out, and_3_out, and_4_out);
  or or_3 (or_3_out, and_5_out, and_6_out);
  or or_4 (or_4_out, and_7_out, and_8_out);
  or or_5 (or_5_out, and_9_out, and_10_out);
  or or_6 (or_6_out, or_1_out, or_2_out);
  or or_7 (or_7_out, or_4_out, or_5_out);
  or or_8 (or_8_out, or_3_out, or_7_out);
  or or_9 (out_5, or_6_out, or_8_out);

  // Notes on the sheet:
  //   D) (y' . w . z') + (x' . y . w') + (y . w' . z') + (x' . y ) + (y . w ) + (y . w) + (x' . z) + (x. w . z') + (x . y . z') + ( w . z')
endmodule

module Guia0603_E (
  input  X,
  input  Y,
  input  W,
  input  Z,
  output out_5
);

  wire and_1_out, and_2_out, and_3_out, and_4_out, and_5_out, and_6_out, and_7_out, and_8_out, and_9_out,
       and_10_out, not_1_out, not_2_out, not_3_out, not_4_out, not_5_out, not_6_out, not_7_out, not_8_out,
       not_9_out, not_10_out, not_11_out, not_12_out, not_13_out, not_14_out, not_15_out, not_16_out,
       not_17_out, not_18_out, or_1_out, or_2_out, or_3_out, or_4_out, or_5_out, or_6_out, or_7_out, or_8_out;

  not not_1 (not_1_out, X);
  not not_2 (not_2_out, Y);
  not not_3 (not_3_out, W);
  not not_4 (not_4_out, Y);
  not not_5 (not_5_out, W);
  not not_6 (not_6_out, Y);
  not not_7 (not_7_out, W);
  not not_8 (not_8_out, Y);
  not not_9 (not_9_out, W);
  not not_10 (not_10_out, Y);
  not not_11 (not_11_out, W);
  not not_12 (not_12_out, Z);
  not not_13 (not_13_out, Y);
  not not_14 (not_14_out, W);
  not not_15 (not_15_out, W);
  not not_16 (not_16_out, Z);
  not not_17 (not_17_out, W);
  not not_18 (not_18_out, Z);
  and and_1 (and_1_out, not_1_out, not_2_out, not_3_out);
  and and_2 (and_2_out, X, not_4_out, not_5_out);
  and and_3 (and_3_out, not_6_out, not_7_out);
  and and_4 (and_4_out, not_8_out, not_9_out, Z);
  and and_5 (and_5_out, not_10_out, not_11_out, not_12_out);
  and and_6 (and_6_out, not_13_out, not_14_out);
  and and_7 (and_7_out, Y, W);
  and and_8 (and_8_out, not_15_out, not_16_out);
  and and_9 (and_9_out, X, not_17_out, not_18_out);
  and and_10 (and_10_out, X, Y);
  or or_1 (or_1_out, and_1_out, and_2_out);
  or or_2 (or_2_out, and_3_out, and_4_out);
  or or_3 (or_3_out, and_5_out, and_6_out);
  or or_4 (or_4_out, and_7_out, and_8_out);
  or or_5 (or_5_out, and_9_out, and_10_out);
  or or_6 (or_6_out, or_1_out, or_2_out);
  or or_7 (or_7_out, or_4_out, or_5_out);
  or or_8 (or_8_out, or_3_out, or_7_out);
  or or_9 (out_5, or_6_out, or_8_out);

  // Notes on the sheet:
  //   E) (x' . y' . w') + (x . y' . w' ) + ( y' . w') + ( y' . w' . z') + ( y' . w' . z') + ( y' . w')+ (y . w ) +(w' . z') + (x . w' . z') + (x . y )
endmodule

module Guia0604_A (
  input  X,
  input  Y,
  input  W,
  input  Z,
  output out_5
);

  wire not_1_out, not_2_out, not_3_out, not_4_out, or_1_out, or_2_out;

  not not_1 (not_1_out, Y);
  not not_2 (not_2_out, Z);
  not not_3 (not_3_out, Y);
  not not_4 (not_4_out, Z);
  or or_1 (or_1_out, X, not_1_out, not_2_out);
  or or_2 (or_2_out, not_3_out, W, not_4_out);
  and and_1 (out_5, or_1_out, or_2_out);

  // Notes on the sheet:
  //   A) (X + Y' + Z') . (Y' + W + Z')
endmodule

module Guia0604_B (
  input  X,
  input  Y,
  input  W,
  input  Z,
  output out_5
);

  wire and_1_out, and_2_out, and_3_out, and_4_out, and_5_out, and_6_out, not_1_out, not_2_out, not_3_out,
       or_1_out, or_2_out, or_3_out, or_4_out, or_5_out, or_6_out, or_7_out, or_8_out;

  not not_1 (not_1_out, Y);
  not not_2 (not_2_out, X);
  not not_3 (not_3_out, X);
  or or_1 (or_1_out, not_1_out, W, Z);
  or or_2 (or_2_out, not_2_out, Y, W);
  or or_3 (or_3_out, Y, W);
  or or_4 (or_4_out, Y, W);
  or or_5 (or_5_out, not_3_out, Z);
  or or_6 (or_6_out, W, Z);
  or or_7 (or_7_out, W, Z);
  or or_8 (or_8_out, W, Z);
  and and_1 (and_1_out, or_1_out, or_2_out);
  and and_2 (and_2_out, or_3_out, or_4_out);
  and and_3 (and_3_out, or_5_out, or_6_out);
  and and_4 (and_4_out, or_7_out, or_8_out);
  and and_5 (and_5_out, and_1_out, and_2_out);
  and and_6 (and_6_out, and_3_out, and_4_out);
  and and_7 (out_5, and_5_out, and_6_out);

  // Notes on the sheet:
  //   B) (Y' + W + Z) . (X' + Y + W ) . (Y + W) . (Y + W) . (X'+ Z) . (W + Z) . ( W + Z) . ( W + Z)
endmodule

module Guia0604_C (
  input  X,
  input  Y,
  input  W,
  input  Z,
  output out_5
);

  wire and_1_out, and_2_out, and_3_out, not_1_out, not_2_out, not_3_out, not_4_out, not_5_out, not_6_out,
       not_7_out, or_1_out, or_2_out, or_3_out, or_4_out, or_5_out;

  not not_1 (not_1_out, Y);
  not not_2 (not_2_out, X);
  not not_3 (not_3_out, Y);
  not not_4 (not_4_out, Y);
  not not_5 (not_5_out, X);
  not not_6 (not_6_out, Y);
  not not_7 (not_7_out, Z);
  or or_1 (or_1_out, not_1_out, W, Z);
  or or_2 (or_2_out, not_2_out, not_3_out, W);
  or or_3 (or_3_out, W, Z);
  or or_4 (or_4_out, not_4_out, W);
  or or_5 (or_5_out, not_5_out, not_6_out, not_7_out);
  and and_1 (and_1_out, or_1_out, or_2_out);
  and and_2 (and_2_out, or_3_out, or_4_out);
  and and_3 (and_3_out, and_2_out, or_5_out);
  and and_4 (out_5, and_1_out, and_3_out);

  // Notes on the sheet:
  //   C) (Y' + W + Z) . (X' + Y' + W ) . (W + Z) . (Y' + W) . (X' + Y' + Z')
endmodule

module Guia0604_D (
  input  X,
  input  Y,
  input  W,
  input  Z,
  output out_5
);

  wire and_1_out, and_2_out, and_3_out, and_4_out, not_1_out, not_2_out, not_3_out, not_4_out, not_5_out,
       not_6_out, not_7_out, not_8_out, not_9_out, not_10_out, or_1_out, or_2_out, or_3_out, or_4_out,
       or_5_out, or_6_out;

  not not_1 (not_1_out, Y);
  not not_2 (not_2_out, Z);
  not not_3 (not_3_out, Z);
  not not_4 (not_4_out, Z);
  not not_5 (not_5_out, X);
  not not_6 (not_6_out, Y);
  not not_7 (not_7_out, Z);
  not not_8 (not_8_out, Y);
  not not_9 (not_9_out, W);
  not not_10 (not_10_out, Z);
  or or_1 (or_1_out, X, Y);
  or or_2 (or_2_out, X, not_1_out, not_2_out);
  or or_3 (or_3_out, W, not_3_out);
  or or_4 (or_4_out, W, not_4_out);
  or or_5 (or_5_out, not_5_out, not_6_out, not_7_out);
  or or_6 (or_6_out, not_8_out, not_9_out, not_10_out);
  and and_1 (and_1_out, or_1_out, or_2_out);
  and and_2 (and_2_out, or_3_out, or_4_out);
  and and_3 (and_3_out, or_5_out, or_6_out);
  and and_4 (and_4_out, and_1_out, and_2_out);
  and and_5 (out_5, and_4_out, and_3_out);

  // Notes on the sheet:
  //   D) (X + Y) . ( X + Y' + Z') . ( W + Z') . (W + Z') . (X' + Y' + Z') . (Y' + W' + Z')
endmodule

module Guia0604_E (
  input  X,
  input  Y,
  input  W,
  input  Z,
  output out_5
);

  wire and_1_out, and_2_out, and_3_out, and_4_out, and_5_out, not_1_out, not_2_out, not_3_out, not_4_out,
       not_5_out, not_6_out, not_7_out, not_8_out, not_9_out, not_10_out, not_11_out, not_12_out, not_13_out,
       or_1_out, or_2_out, or_3_out, or_4_out, or_5_out, or_6_out, or_7_out;

  not not_1 (not_1_out, Y);
  not not_2 (not_2_out, Y);
  not not_3 (not_3_out, W);
  not not_4 (not_4_out, Y);
  not not_5 (not_5_out, Y);
  not not_6 (not_6_out, Y);
  not not_7 (not_7_out, W);
  not not_8 (not_8_out, X);
  not not_9 (not_9_out, Y);
  not not_10 (not_10_out, W);
  not not_11 (not_11_out, Y);
  not not_12 (not_12_out, W);
  not not_13 (not_13_out, Z);
  or or_1 (or_1_out, X, not_1_out, W);
  or or_2 (or_2_out, X, not_2_out, not_3_out);
  or or_3 (or_3_out, X, not_4_out);
  or or_4 (or_4_out, X, not_5_out);
  or or_5 (or_5_out, not_6_out, not_7_out, Z);
  or or_6 (or_6_out, not_8_out, not_9_out, not_10_out);
  or or_7 (or_7_out, not_11_out, not_12_out, not_13_out);
  and and_1 (and_1_out, or_1_out, or_2_out);
  and and_2 (and_2_out, or_3_out, or_4_out);
  and and_3 (and_3_out, or_5_out, or_6_out);
  and and_4 (and_4_out, and_1_out, and_2_out);
  and and_5 (and_5_out, and_3_out, or_7_out);
  and and_6 (out_5, and_4_out, and_5_out);

  // Notes on the sheet:
  //   E) ( X + Y' + W) . (X + Y' + W') . (X + Y') . (X + Y') . (Y' + W' + Z) . (X' + Y' + W' ) .( Y' + W' + Z')
endmodule

module Guia0605 (
  input  X,
  input  Y,
  input  Z,
  output out_4,
  output out_5
);

  wire and_1_out, and_2_out, and_3_out, and_4_out, not_1_out, not_2_out, not_3_out, not_4_out, not_5_out,
       not_6_out, or_1_out, or_3_out;

  not not_1 (not_1_out, X);
  not not_2 (not_2_out, Y);
  or or_1 (or_1_out, not_1_out, not_2_out);
  and and_1 (and_1_out, X, Y);
  and and_2 (and_2_out, Y, Z);
  not not_3 (not_3_out, X);
  and and_3 (and_3_out, Y, Z);
  not not_4 (not_4_out, or_1_out);
  not not_5 (not_5_out, and_1_out);
  not not_6 (not_6_out, X);
  or or_2 (out_5, not_3_out, and_3_out);
  and and_4 (and_4_out, not_4_out, not_5_out);
  or or_3 (or_3_out, and_2_out, not_6_out);
  or or_4 (out_4, and_4_out, or_3_out);

  // Notes on the sheet:
  //   Expressão SImplificada (A'+B.C)
  //   ExpressãoOriginal ((X' + Y')' . (X . Y)' + ((Y Z) + X')')
endmodule

module Guia0606 (
  input  X,
  input  Y,
  input  W,
  input  Z,
  output out_5,
  output out_6
);

  wire and_1_out, and_2_out, and_3_out, and_4_out, and_5_out, and_6_out, not_1_out, not_2_out, not_3_out,
       not_4_out, not_5_out, not_6_out, not_7_out, not_8_out, not_9_out, not_10_out, not_11_out, not_12_out,
       not_13_out, not_14_out, not_15_out, or_1_out, or_2_out, or_3_out, or_4_out, or_5_out, or_6_out,
       or_7_out;

  not not_1 (not_1_out, X);
  or or_1 (or_1_out, not_1_out, not_2_out, W);
  not not_2 (not_2_out, Y);
  and and_1 (and_1_out, X, Y, not_3_out);
  not not_3 (not_3_out, W);
  and and_2 (and_2_out, Y, W, Z);
  not not_4 (not_4_out, X);
  not not_5 (not_5_out, X);
  or or_2 (or_2_out, not_5_out, not_6_out);
  not not_6 (not_6_out, Y);
  not not_7 (not_7_out, X);
  or or_3 (or_3_out, not_7_out, Y);
  or or_4 (or_4_out, W, not_8_out);
  not not_8 (not_8_out, Z);
  not not_9 (not_9_out, X);
  or or_5 (or_5_out, not_9_out, not_10_out, Z);
  not not_10 (not_10_out, W);
  not not_11 (not_11_out, X);
  or or_6 (or_6_out, not_11_out, W, not_12_out);
  not not_12 (not_12_out, Z);
  not not_13 (not_13_out, or_1_out);
  not not_14 (not_14_out, and_1_out);
  and and_3 (and_3_out, not_13_out, not_14_out);
  not not_15 (not_15_out, or_7_out);
  or or_7 (or_7_out, and_2_out, not_4_out);
  and and_4 (and_4_out, or_2_out, or_3_out);
  and and_5 (and_5_out, or_4_out, or_5_out);
  or or_8 (out_5, and_3_out, not_15_out);
  and and_6 (and_6_out, and_4_out, and_5_out);
  and and_7 (out_6, and_6_out, or_6_out);
endmodule
