// Logisim project Guia0702.circ as structural Verilog
module Guia0701 (
  input  A,
  input  B,
  input  C,
  output out_4,
  output out_5,
  output out_6
);

  and and_1 (out_4, A, B);
  nand nand_1 (out_6, A, B);
  Multiplexer multiplexer_1 (.in0(out_4), .in1(out_6), .out(out_5), .sel(C));  // open: en
endmodule

module Guia0702 (
  input  A,
  input  B,
  input  C,
  output out_4,
  output out_5,
  output out_6
);

  or or_1 (out_6, A, B);
  nor nor_1 (out_4, A, B);
  Multiplexer multiplexer_1 (.in0(out_4), .in1(out_6), .out(out_5), .sel(C));  // open: en
endmodule

module Guia0703 (
  input  A,
  input  B,
  input  C,
  input  C_2,
  input  C_3,
  output out_6,
  output out_7,
  output out_8
);

  wire multiplexer_1_out, multiplexer_2_out, nor_1_out, or_1_out;

  and and_1 (out_6, A, B);
  or or_1 (or_1_out, A, B);
  nand nand_1 (out_7, A, B);
  nor nor_1 (nor_1_out, A, B);
  Multiplexer multiplexer_1 (.in0(out_7), .in1(out_6), .out(multiplexer_1_out), .sel(C));  // open: en
  Multiplexer multiplexer_2 (.in0(nor_1_out), .in1(or_1_out), .out(multiplexer_2_out), .sel(C_3));  // open: en
  Multiplexer multiplexer_3 (.in0(multiplexer_1_out), .in1(multiplexer_2_out), .out(out_8), .sel(C_2));  // open: en
endmodule

module Guia0704 (
  input  A,
  input  B,
  input  [1:0] C,
  output out_4
);

  wire nor_1_out, or_1_out, xnor_1_out, xor_1_out;

  xnor xnor_1 (xnor_1_out, A, B);
  xor xor_1 (xor_1_out, A, B);
  nor nor_1 (nor_1_out, A, B);
  or or_1 (or_1_out, A, B);
  Multiplexer #(.select(2)) multiplexer_1 (
    .in0(xnor_1_out), .in1(xor_1_out), .in2(nor_1_out), .in3(or_1_out), .out(out_4), .sel(C));  // open: en
endmodule

module Guia0705 (
  input  A,
  input  B,
  input  [2:0] C,
  output out_4
);

  wire and_1_out, nand_1_out, nor_1_out, not_1_out, not_2_out, or_1_out, xnor_1_out, xor_1_out;

  not not_1 (not_1_out, A);
  not not_2 (not_2_out, B);
  and and_1 (and_1_out, A, B);
  nand nand_1 (nand_1_out, A, B);
  xor xor_1 (xor_1_out, A, B);
  xnor xnor_1 (xnor_1_out, A, B);
  or or_1 (or_1_out, A, B);
  nor nor_1 (nor_1_out, A, B);
  Multiplexer #(.select(3)) multiplexer_1 (
    .in0(not_1_out), .in1(not_2_out), .in2(and_1_out), .in3(nand_1_out), .in4(xor_1_out), .in5(xnor_1_out),
    .in6(or_1_out), .in7(nor_1_out), .out(out_4), .sel(C));  // open: en
endmodule
