// Logisim project Guia0801(SomadorCompleto).circ as structural Verilog: 3 circuits, main circuit Meia-soma
module Meia_soma (
  input  A,
  input  B,
  output s,
  output V
);

  wire and_1_out, and_2_out, not_1_out, not_2_out;

  not not_1 (not_1_out, A);
  not not_2 (not_2_out, B);
  and and_1 (and_1_out, not_1_out, B);
  and and_2 (and_2_out, A, not_2_out);
  and and_3 (V, A, B);
  or or_1 (s, and_1_out, and_2_out);

  // Notes on the sheet:
  //   V= (a.b)
  //   S= (a'.b) + (a.b')
endmodule

// SC (+)
module Soma_completa (
  input  A,
  input  B,
  input  Vem_um__carry_in,
  output S,
  output Vai_um__carry_out
);

  wire meia_soma_1_s, meia_soma_1_v, meia_soma_2_v;

  Meia_soma meia_soma_1 (.s(meia_soma_1_s), .V(meia_soma_1_v), .A(A), .B(B));
  Meia_soma meia_soma_2 (.s(S), .V(meia_soma_2_v), .A(Vem_um__carry_in), .B(meia_soma_1_s));
  or or_1 (Vai_um__carry_out, meia_soma_2_v, meia_soma_1_v);
endmodule

module Circuito_Principal (
  input  A3,
  input  B3,
  input  A2,
  input  B2,
  input  A1,
  input  B1,
  input  A0,
  input  B0,
  output S3,
  output S2,
  output S1,
  output S0
);

  wire soma_completa_2_vai_um__carry_out, soma_completa_3_vai_um__carry_out,
       soma_completa_4_vai_um__carry_out;

  Soma_completa soma_completa_1 (
    .S(S3), .A(A3), .B(B3), .Vem_um__carry_in(soma_completa_2_vai_um__carry_out));  // open: Vai_um__carry_out
  Soma_completa soma_completa_2 (
    .S(S2), .Vai_um__carry_out(soma_completa_2_vai_um__carry_out), .A(A2), .B(B2),
    .Vem_um__carry_in(soma_completa_3_vai_um__carry_out));
  Soma_completa soma_completa_3 (
    .S(S1), .Vai_um__carry_out(soma_completa_3_vai_um__carry_out), .A(A1), .B(B1),
    .Vem_um__carry_in(soma_completa_4_vai_um__carry_out));
  Soma_completa soma_completa_4 (
    .S(S0), .Vai_um__carry_out(soma_completa_4_vai_um__carry_out), .A(A0), .B(B0), .Vem_um__carry_in(1'b0));
endmodule
