// Logisim project Guia0802(SubtratorCompleto).circ as structural Verilog: 3 circuits, main circuit Meia-Subtração
module \Meia_Subtração  (
  input  A,
  input  B,
  output s,
  output V
);

  wire and_1_out, and_2_out, not_1_out, not_2_out, not_3_out;

  not not_1 (not_1_out, A);
  not not_2 (not_2_out, B);
  not not_3 (not_3_out, A);
  and and_1 (and_1_out, not_1_out, B);
  and and_2 (and_2_out, A, not_2_out);
  and and_3 (V, not_3_out, B);
  or or_1 (s, and_1_out, and_2_out);

  // Notes on the sheet:
  //   V= (a'.b)
  //   S= (a'.b) + (a.b')
endmodule

// SC (-)
module \Subtração_completa  (
  input  A,
  input  B,
  input  Emprestado__borrow,
  output S,
  output V__Empresta
);

  wire \meia_subtração_1_s , \meia_subtração_1_v , \meia_subtração_2_v ;

  \Meia_Subtração  \meia_subtração_1  (.s(\meia_subtração_1_s ), .V(\meia_subtração_1_v ), .A(A), .B(B));
  \Meia_Subtração  \meia_subtração_2  (
    .s(S), .V(\meia_subtração_2_v ), .A(Emprestado__borrow), .B(\meia_subtração_1_s ));
  or or_1 (V__Empresta, \meia_subtração_2_v , \meia_subtração_1_v );
endmodule

module Circuito_Principal (
  input  A3,
  input  B3,
  input  A2,
  input  B2,
  input  A1,
  input  B1,
  input  A0,
  input  B0,
  input  Empresta,
  output S3,
  output S2,
  output S1,
  output S0
);

  wire \subtração_completa_2_v__empresta , \subtração_completa_3_v__empresta ,
       \subtração_completa_4_v__empresta ;

  \Subtração_completa  \subtração_completa_1  (
    .S(S3), .V__Empresta(Empresta), .A(A3), .B(B3), .Emprestado__borrow(\subtração_completa_2_v__empresta ));
  \Subtração_completa  \subtração_completa_2  (
    .S(S2), .V__Empresta(\subtração_completa_2_v__empresta ), .A(A2), .B(B2),
    .Emprestado__borrow(\subtração_completa_3_v__empresta ));
  \Subtração_completa  \subtração_completa_3  (
    .S(S1), .V__Empresta(\subtração_completa_3_v__empresta ), .A(A1), .B(A1),
    .Emprestado__borrow(\subtração_completa_4_v__empresta ));
  \Subtração_completa  \subtração_completa_4  (
    .S(S0), .V__Empresta(\subtração_completa_4_v__empresta ), .A(A0), .B(B0), .Emprestado__borrow(1'b0));

  assign B1 = A1;
endmodule
