// Logisim project Guia0803(ComparadorIgualdade).circ as structural Verilog: 2 circuits, main circuit Comparador de Igualdade
// CMP ==
module Comparador_de_Igualdade (
  input  A,
  input  B,
  output out_3
);

  xnor xnor_1 (out_3, A, B);
endmodule

module Circuito_Principal (
  input  A3,
  input  B3,
  input  A2,
  input  B2,
  input  A1,
  input  B1,
  input  A0,
  input  B0,
  output S0,
  output S0_2,
  output S0_3,
  output S0_4
);

  Comparador_de_Igualdade comparador_de_igualdade_1 (.out_3(S0_3), .A(A3), .B(B3));
  Comparador_de_Igualdade comparador_de_igualdade_2 (.out_3(S0_4), .A(A2), .B(B2));
  Comparador_de_Igualdade comparador_de_igualdade_3 (.out_3(S0), .A(A1), .B(B1));
  Comparador_de_Igualdade comparador_de_igualdade_4 (.out_3(S0_2), .A(A0), .B(B0));
endmodule
