// Logisim project Guia0805(Complemento2).circ as structural Verilog: 3 circuits, main circuit Meio-Somador
module Meio_Somador (
  input  A,
  input  B,
  output s,
  output V
);

  wire and_1_out, and_2_out, not_1_out, not_2_out;

  not not_1 (not_1_out, A);
  not not_2 (not_2_out, B);
  and and_1 (and_1_out, not_1_out, B);
  and and_2 (and_2_out, A, not_2_out);
  and and_3 (V, A, B);
  or or_1 (s, and_1_out, and_2_out);

  // Notes on the sheet:
  //   V= (a.b)
  //   S= (a'.b) + (a.b')
endmodule

// SC
module Somador_Completo (
  input  A,
  input  B,
  input  Vem_um__carry_in,
  output S,
  output Vai_Um__carry_out
);

  wire meio_somador_1_s, meio_somador_1_v, meio_somador_2_v;

  Meio_Somador meio_somador_1 (.s(meio_somador_1_s), .V(meio_somador_1_v), .A(A), .B(B));
  Meio_Somador meio_somador_2 (.s(S), .V(meio_somador_2_v), .A(Vem_um__carry_in), .B(meio_somador_1_s));
  or or_1 (Vai_Um__carry_out, meio_somador_2_v, meio_somador_1_v);
endmodule

module Circuito_Principal (
  input  A3,
  input  A2,
  input  A1,
  input  A0,
  output S3,
  output S2,
  output S1,
  output S0
);

  wire somador_completo_1_vai_um__carry_out, somador_completo_2_vai_um__carry_out,
       somador_completo_3_vai_um__carry_out, somador_completo_4_vai_um__carry_out;

  Somador_Completo somador_completo_1 (
    .S(S3), .Vai_Um__carry_out(somador_completo_1_vai_um__carry_out), .A(A3), .B(1'b0),
    .Vem_um__carry_in(somador_completo_2_vai_um__carry_out));
  Somador_Completo somador_completo_2 (
    .S(S2), .Vai_Um__carry_out(somador_completo_2_vai_um__carry_out), .A(A2), .B(1'b0),
    .Vem_um__carry_in(somador_completo_3_vai_um__carry_out));
  Somador_Completo somador_completo_3 (
    .S(S1), .Vai_Um__carry_out(somador_completo_3_vai_um__carry_out), .A(A1), .B(1'b0),
    .Vem_um__carry_in(somador_completo_4_vai_um__carry_out));
  Somador_Completo somador_completo_4 (
    .S(S0), .Vai_Um__carry_out(somador_completo_4_vai_um__carry_out), .A(A0), .B(1'b0),
    .Vem_um__carry_in(1'b1));
  // also tied to GND on the sheet: somador_completo_1_vai_um__carry_out
endmodule
