// Logisim project Guia1201.circ as structural Verilog: 3 circuits, main circuit main
module main (
  input  Adress,
  input  R_W,
  input  Clear,
  input  [3:0] Entrada,
  output [3:0] Saida
);

  wire and_2_out, j_k_ff_1_q, j_k_ff_2_q, j_k_ff_3_q, j_k_ff_4_q, not_1_out, not_2_out, not_3_out, not_4_out;
  wire [2:2] clock_1_out;
  wire [3:0] controlled_buffer_1_out;

  Clock clock_1 (.out(clock_1_out[2]));
  assign controlled_buffer_1_out = R_W ? Entrada : 4'bz;  // Controlled_Buffer controlled_buffer_1
  and and_1 (Saida[0], j_k_ff_1_q, Adress);
  and and_2 (and_2_out, Adress, R_W, clock_1_out[2]);
  not not_1 (not_1_out, controlled_buffer_1_out[0]);
  and and_3 (Saida[1], j_k_ff_2_q, Adress);
  J_K_Flip_Flop j_k_ff_1 (
    .J(controlled_buffer_1_out[0]), .clk(and_2_out), .K(not_1_out), .Q(j_k_ff_1_q), .reset(Clear));  // open: Qn, preset, en
  and and_4 (Saida[2], j_k_ff_3_q, Adress);
  not not_2 (not_2_out, controlled_buffer_1_out[1]);
  and and_5 (Saida[3], j_k_ff_4_q, Adress);
  J_K_Flip_Flop j_k_ff_2 (
    .J(controlled_buffer_1_out[1]), .clk(and_2_out), .K(not_2_out), .Q(j_k_ff_2_q), .reset(Clear));  // open: Qn, preset, en
  J_K_Flip_Flop j_k_ff_3 (
    .J(controlled_buffer_1_out[2]), .clk(and_2_out), .K(not_3_out), .Q(j_k_ff_3_q), .reset(Clear));  // open: Qn, preset, en
  not not_3 (not_3_out, controlled_buffer_1_out[2]);
  not not_4 (not_4_out, controlled_buffer_1_out[3]);
  J_K_Flip_Flop j_k_ff_4 (
    .J(controlled_buffer_1_out[3]), .clk(and_2_out), .K(not_4_out), .Q(j_k_ff_4_q), .reset(Clear));  // open: Qn, preset, en
endmodule

// 1x2
module Guia1202 (
  input  Adress,
  input  CLK,
  input  RW,
  input  Clear,
  input  [1:0] Entrada,
  output [1:0] Saida
);

  wire and_1_out, j_k_ff_1_q, j_k_ff_2_q, not_1_out, not_2_out;
  wire [1:0] controlled_buffer_1_out;

  assign controlled_buffer_1_out = CLK ? Entrada : 2'bz;  // Controlled_Buffer controlled_buffer_1
  and and_1 (and_1_out, Adress, CLK, RW);
  not not_1 (not_1_out, controlled_buffer_1_out[0]);
  assign Saida[0] = Adress ? j_k_ff_1_q : 1'bz;  // Controlled_Buffer controlled_buffer_2
  J_K_Flip_Flop j_k_ff_1 (
    .J(controlled_buffer_1_out[0]), .clk(and_1_out), .K(not_1_out), .Q(j_k_ff_1_q), .reset(Clear));  // open: Qn, preset, en
  not not_2 (not_2_out, controlled_buffer_1_out[1]);
  assign Saida[1] = Adress ? j_k_ff_2_q : 1'bz;  // Controlled_Buffer controlled_buffer_3
  J_K_Flip_Flop j_k_ff_2 (
    .J(controlled_buffer_1_out[1]), .clk(and_1_out), .K(not_2_out), .Q(j_k_ff_2_q), .reset(Clear));  // open: Qn, preset, en
endmodule

module _1202Main (
  input  Adress,
  input  CLK,
  input  RW,
  input  [3:0] in_4,
  input  Clear,
  output [3:0] out_6
);

  Guia1202 guia1202_1 (.Adress(Adress), .CLK(CLK), .RW(RW), .Clear(Clear), .Entrada(in_4[1:0]), .Saida(out_6[1:0]));
  Guia1202 guia1202_2 (.Adress(Adress), .CLK(CLK), .RW(RW), .Clear(Clear), .Entrada(in_4[3:2]), .Saida(out_6[3:2]));
endmodule
