// Logisim project Guia1204.circ as structural Verilog: 5 circuits, main circuit main
module main (
  input  Adress,
  input  R_W,
  input  Clear,
  input  [3:0] Entrada,
  output [3:0] Saida
);

  wire and_2_out, j_k_ff_1_q, j_k_ff_2_q, j_k_ff_3_q, j_k_ff_4_q, not_1_out, not_2_out, not_3_out, not_4_out;
  wire [2:2] clock_1_out;
  wire [3:0] controlled_buffer_1_out;

  Clock clock_1 (.out(clock_1_out[2]));
  assign controlled_buffer_1_out = R_W ? Entrada : 4'bz;  // Controlled_Buffer controlled_buffer_1
  and and_1 (Saida[0], j_k_ff_1_q, Adress);
  and and_2 (and_2_out, Adress, R_W, clock_1_out[2]);
  not not_1 (not_1_out, controlled_buffer_1_out[0]);
  and and_3 (Saida[1], j_k_ff_2_q, Adress);
  J_K_Flip_Flop j_k_ff_1 (
    .J(controlled_buffer_1_out[0]), .clk(and_2_out), .K(not_1_out), .Q(j_k_ff_1_q), .reset(Clear));  // open: Qn, preset, en
  and and_4 (Saida[2], j_k_ff_3_q, Adress);
  not not_2 (not_2_out, controlled_buffer_1_out[1]);
  and and_5 (Saida[3], j_k_ff_4_q, Adress);
  J_K_Flip_Flop j_k_ff_2 (
    .J(controlled_buffer_1_out[1]), .clk(and_2_out), .K(not_2_out), .Q(j_k_ff_2_q), .reset(Clear));  // open: Qn, preset, en
  J_K_Flip_Flop j_k_ff_3 (
    .J(controlled_buffer_1_out[2]), .clk(and_2_out), .K(not_3_out), .Q(j_k_ff_3_q), .reset(Clear));  // open: Qn, preset, en
  not not_3 (not_3_out, controlled_buffer_1_out[2]);
  not not_4 (not_4_out, controlled_buffer_1_out[3]);
  J_K_Flip_Flop j_k_ff_4 (
    .J(controlled_buffer_1_out[3]), .clk(and_2_out), .K(not_4_out), .Q(j_k_ff_4_q), .reset(Clear));  // open: Qn, preset, en
endmodule

// 1x2
module Guia1202 (
  input  Adress,
  input  CLK,
  input  RW,
  input  Clear,
  input  [1:0] Entrada,
  output [1:0] Saida
);

  wire and_1_out, j_k_ff_1_q, j_k_ff_2_q, not_1_out, not_2_out;
  wire [1:0] controlled_buffer_1_out;

  assign controlled_buffer_1_out = CLK ? Entrada : 2'bz;  // Controlled_Buffer controlled_buffer_1
  and and_1 (and_1_out, Adress, CLK, RW);
  not not_1 (not_1_out, controlled_buffer_1_out[0]);
  assign Saida[0] = Adress ? j_k_ff_1_q : 1'bz;  // Controlled_Buffer controlled_buffer_2
  J_K_Flip_Flop j_k_ff_1 (
    .J(controlled_buffer_1_out[0]), .clk(and_1_out), .K(not_1_out), .Q(j_k_ff_1_q), .reset(Clear));  // open: Qn, preset, en
  not not_2 (not_2_out, controlled_buffer_1_out[1]);
  assign Saida[1] = Adress ? j_k_ff_2_q : 1'bz;  // Controlled_Buffer controlled_buffer_3
  J_K_Flip_Flop j_k_ff_2 (
    .J(controlled_buffer_1_out[1]), .clk(and_1_out), .K(not_2_out), .Q(j_k_ff_2_q), .reset(Clear));  // open: Qn, preset, en
endmodule

// 1x4
module _1202Main (
  input  Adress,
  input  CLK,
  input  RW,
  input  [3:0] in_4,
  input  Clear,
  output [3:0] out_6
);

  Guia1202 guia1202_1 (.Adress(Adress), .CLK(CLK), .RW(RW), .Clear(Clear), .Entrada(in_4[1:0]), .Saida(out_6[1:0]));
  Guia1202 guia1202_2 (.Adress(Adress), .CLK(CLK), .RW(RW), .Clear(Clear), .Entrada(in_4[3:2]), .Saida(out_6[3:2]));
endmodule

// 2x4
module Guia1203 (
  input  in_1,
  input  RW,
  input  CLK,
  input  Clear,
  input  [3:0] Entrada,
  output [3:0] Saida
);

  wire demultiplexer_1_out0, demultiplexer_1_out1, undriven;
  wire [3:0] n1202main_1_out_6, n1202main_2_out_6;

  _1202Main u_1202main_1 (
    .Adress(demultiplexer_1_out0), .CLK(CLK), .RW(RW), .Clear(Clear), .out_6(n1202main_1_out_6),
    .in_4(Entrada));
  _1202Main u_1202main_2 (
    .Adress(demultiplexer_1_out1), .CLK(CLK), .RW(RW), .Clear(Clear), .out_6(n1202main_2_out_6),
    .in_4(Entrada));
  Demultiplexer demultiplexer_1 (
    .out0(demultiplexer_1_out0), .out1(demultiplexer_1_out1), .in(in_1), .sel(undriven));  // open: en
  Multiplexer #(.width(4)) multiplexer_1 (
    .in0(n1202main_1_out_6), .in1(n1202main_2_out_6), .out(Saida), .sel(undriven));  // open: en
endmodule

module Guia1204 (
  input  RW,
  input  [1:0] Adress,
  input  CLK,
  input  [7:0] Entrada,
  input  clear,
  output [7:0] Saida
);

  wire demultiplexer_1_out0, demultiplexer_1_out1, demultiplexer_1_out2, demultiplexer_1_out3;

  Guia1203 guia1203_1 (
    .RW(RW), .CLK(CLK), .Clear(clear), .in_1(demultiplexer_1_out0), .Saida(Entrada[3:0]),
    .Entrada(Entrada[7:4]));
  Guia1203 guia1203_2 (
    .RW(RW), .Clear(clear), .in_1(demultiplexer_1_out0), .Saida(Entrada[3:0]), .Entrada(Entrada[7:4]));  // open: CLK
  Guia1203 guia1203_3 (
    .RW(RW), .CLK(CLK), .Clear(clear), .in_1(demultiplexer_1_out1), .Saida(Entrada[3:0]),
    .Entrada(Entrada[7:4]));
  Guia1203 guia1203_4 (
    .RW(RW), .CLK(CLK), .Clear(clear), .in_1(demultiplexer_1_out1), .Saida(Entrada[3:0]),
    .Entrada(Entrada[7:4]));
  Guia1203 guia1203_5 (
    .RW(RW), .CLK(CLK), .Clear(clear), .in_1(demultiplexer_1_out2), .Saida(Entrada[3:0]),
    .Entrada(Entrada[7:4]));
  Guia1203 guia1203_6 (
    .RW(RW), .CLK(CLK), .Clear(clear), .in_1(demultiplexer_1_out2), .Saida(Entrada[3:0]),
    .Entrada(Entrada[7:4]));
  Guia1203 guia1203_7 (
    .RW(RW), .CLK(CLK), .Clear(clear), .in_1(demultiplexer_1_out3), .Saida(Entrada[3:0]),
    .Entrada(Entrada[7:4]));
  Guia1203 guia1203_8 (
    .RW(RW), .CLK(CLK), .Clear(clear), .in_1(demultiplexer_1_out3), .Saida(Entrada[3:0]),
    .Entrada(Entrada[7:4]));
  Demultiplexer #(.select(2)) demultiplexer_1 (
    .out0(demultiplexer_1_out0), .out1(demultiplexer_1_out1), .out2(demultiplexer_1_out2),
    .out3(demultiplexer_1_out3), .in(1'b1), .sel(Adress));  // open: en
  Multiplexer #(.select(2), .width(2)) multiplexer_1 (
    .in0({2{Entrada[0]}}), .in1({2{Entrada[0]}}), .in2({2{Entrada[0]}}), .in3({2{Entrada[0]}}),
    .out(Saida[1:0]), .en(Adress[0]));  // open: sel
  // Pins of 1 and 4 bits meet at Entrada[3:0]
  // Pins of 1 and 2 bits meet at Adress
  // Pins of 2 and 8 bits meet at Saida
endmodule
