// Logisim project Exemplo_1301.circ as structural Verilog
module Exemplo_1301 (
  input  Pulso,
  input  _1,
  input  Clear,
  output A,
  output B,
  output C,
  output D
);

  J_K_Flip_Flop j_k_ff_1 (.J(_1), .clk(B), .K(_1), .Qn(A), .reset(Clear));  // open: Q, preset, en
  J_K_Flip_Flop j_k_ff_2 (.J(_1), .clk(C), .K(_1), .Qn(B), .reset(Clear));  // open: Q, preset, en
  J_K_Flip_Flop j_k_ff_3 (.J(_1), .clk(D), .K(_1), .Qn(C), .reset(Clear));  // open: Q, preset, en
  J_K_Flip_Flop j_k_ff_4 (.J(_1), .clk(Pulso), .K(_1), .Qn(D), .reset(Clear));  // open: Q, preset, en
endmodule

module Exemplo_1302 (
  input  Pulso,
  input  _1,
  input  Clear,
  output A,
  output B,
  output C,
  output D
);

  wire j_k_ff_2_q, j_k_ff_3_q, j_k_ff_4_q;

  J_K_Flip_Flop j_k_ff_1 (.J(_1), .clk(j_k_ff_2_q), .K(_1), .Qn(A), .reset(Clear));  // open: Q, preset, en
  J_K_Flip_Flop j_k_ff_2 (.J(_1), .clk(j_k_ff_3_q), .K(_1), .Q(j_k_ff_2_q), .Qn(B), .reset(Clear));  // open: preset, en
  J_K_Flip_Flop j_k_ff_3 (.J(_1), .clk(j_k_ff_4_q), .K(_1), .Q(j_k_ff_3_q), .Qn(C), .reset(Clear));  // open: preset, en
  J_K_Flip_Flop j_k_ff_4 (.J(_1), .clk(Pulso), .K(_1), .Q(j_k_ff_4_q), .Qn(D), .reset(Clear));  // open: preset, en
endmodule

module Exemplo_1304 (
  input  Pulso,
  input  _1,
  output A,
  output B,
  output C,
  output D
);

  wire and_1_out, j_k_ff_1_qn, j_k_ff_2_qn, j_k_ff_3_qn, j_k_ff_4_qn, not_1_out, not_2_out, not_3_out,
       or_1_out;

  not not_1 (not_1_out, _1);
  J_K_Flip_Flop j_k_ff_1 (.J(_1), .clk(Pulso), .K(_1), .Q(D), .Qn(j_k_ff_1_qn), .preset(or_1_out));  // open: en, reset
  or or_1 (or_1_out, not_1_out, and_1_out);
  and and_1 (and_1_out, not_2_out, j_k_ff_2_qn, not_3_out, j_k_ff_4_qn);
  not not_2 (not_2_out, j_k_ff_1_qn);
  not not_3 (not_3_out, j_k_ff_3_qn);
  J_K_Flip_Flop j_k_ff_2 (.J(_1), .clk(D), .K(_1), .Q(C), .Qn(j_k_ff_2_qn), .preset(or_1_out));  // open: en, reset
  J_K_Flip_Flop j_k_ff_3 (.J(_1), .clk(C), .K(_1), .Q(B), .Qn(j_k_ff_3_qn), .preset(or_1_out));  // open: en, reset
  J_K_Flip_Flop j_k_ff_4 (.J(_1), .clk(B), .K(_1), .Q(A), .Qn(j_k_ff_4_qn), .preset(or_1_out));  // open: en, reset
endmodule

module Exemplo_1303 (
  input  Pulso,
  input  _1,
  output A,
  output B,
  output C,
  output D
);

  wire and_1_out, j_k_ff_1_qn, j_k_ff_2_qn, j_k_ff_3_qn, j_k_ff_4_qn, nand_1_out, not_1_out, not_2_out,
       not_3_out;

  not not_1 (not_1_out, _1);
  J_K_Flip_Flop j_k_ff_1 (
    .J(_1), .clk(Pulso), .K(_1), .Q(D), .Qn(j_k_ff_1_qn), .reset(nand_1_out));  // open: preset, en
  nand nand_1 (nand_1_out, not_1_out, and_1_out);
  and and_1 (and_1_out, not_2_out, j_k_ff_2_qn, not_3_out, j_k_ff_4_qn);
  not not_2 (not_2_out, j_k_ff_1_qn);
  not not_3 (not_3_out, j_k_ff_3_qn);
  J_K_Flip_Flop j_k_ff_2 (.J(_1), .clk(D), .K(_1), .Q(C), .Qn(j_k_ff_2_qn), .reset(nand_1_out));  // open: preset, en
  J_K_Flip_Flop j_k_ff_3 (.J(_1), .clk(C), .K(_1), .Q(B), .Qn(j_k_ff_3_qn), .reset(nand_1_out));  // open: preset, en
  J_K_Flip_Flop j_k_ff_4 (.J(_1), .clk(B), .K(_1), .Q(A), .Qn(j_k_ff_4_qn), .reset(nand_1_out));  // open: preset, en
endmodule

module Exemplo_1305 (
  input  Pulso,
  input  Clear,
  output C,
  output B,
  output A
);

  wire and_1_out, not_1_out, or_1_out, t_ff_2_qn, t_ff_3_qn;

  or or_1 (or_1_out, Clear, and_1_out);
  T_Flip_Flop t_ff_1 (.clk(t_ff_2_qn), .T(t_ff_2_qn), .Q(C), .reset(or_1_out));  // open: Qn, preset, en
  and and_1 (and_1_out, C, not_1_out, A);
  not not_1 (not_1_out, B);
  T_Flip_Flop t_ff_2 (.clk(t_ff_3_qn), .T(t_ff_3_qn), .Q(B), .Qn(t_ff_2_qn), .reset(or_1_out));  // open: preset, en
  T_Flip_Flop t_ff_3 (.clk(Pulso), .T(Pulso), .Q(A), .Qn(t_ff_3_qn), .reset(or_1_out));  // open: preset, en
endmodule
